// Logisim project 8_16_computer.circ as structural Verilog: 8 circuits, main circuit main
module main (
  input  in_1
);

  wire ALU_CLR, ALU_NAND, ALU_SUB, and_1_out, and_2_out, ASR_OE, CLK, comparator_1_lt, decoder_1_out0,
       decoder_1_out1, decoder_1_out2, decoder_1_out3, decoder_1_out4, decoder_1_out5, decoder_1_out6,
       decoder_1_out7, decoder_2_out0, decoder_2_out1, decoder_2_out2, decoder_2_out3, decoder_2_out4,
       decoder_2_out5, decoder_2_out6, decoder_2_out7, decoder_3_out0, decoder_3_out1, decoder_3_out2,
       decoder_3_out3, decoder_3_out4, decoder_3_out5, decoder_3_out6, decoder_3_out7, MAR_SEL, n_ALU_CC,
       n_ALU_CS, n_ALU_EN, n_ALU_OE, n_CF, n_CLK, n_CONST_OE_00, n_CONST_OE_FF, n_ED_OE, n_ED_WE, n_IR_WE,
       n_IRX_CLR, n_JCS, n_JEQ, n_JMP, n_MARH_L, n_MARL_L, n_PC_LOAD, n_PCOUT_H, n_PCOUT_L, n_RAM_OE,
       n_RAM_WE, n_RF_OE, n_RF_WE, n_ZF, nor_1_out, nor_2_out, nor_3_out, nor_4_out, nor_5_out, not_1_out,
       not_3_out, not_12_out, not_28_out, not_29_out, not_30_out, not_31_out, not_32_out, not_33_out,
       or_1_out, or_2_out, or_3_out, PC_COUNT, RF_IN_0, RF_IN_1, RF_OUT_0, RF_OUT_1, TTYI, TTYO;
  wire [6:0] bit_extender_1_out, controlled_buffer_5_out, keyboard_1_data, rom_1_data;
  wire [7:0] controlled_buffer_1_out, ledbar_2_p1, ram_1_dout, reg_file_1_ra, reg_file_1_rb, reg_file_1_rc,
       reg_file_1_rd, rom_2_data;
  wire [11:0] ledbar_1_p1;
  wire [15:0] MAR_p1, PC_p1;
  wire [15:2] address_controller_1_addr_out;

  or or_1 (or_1_out, n_CLK, n_IR_WE);
  ROM #(.addrWidth(12), .dataWidth(16)) rom_1 (
    .addr(ledbar_1_p1),
    .data({PC_COUNT, MAR_SEL, RF_OUT_1, RF_OUT_0, RF_IN_1, RF_IN_0, ALU_SUB, ALU_NAND, ALU_CLR, rom_1_data}));
  // LedBar #(.inputtype("row"), .matrixcols(12)) ledbar_1: pin names not known; wires that end beside it: ledbar_1_p1
  // LedBar #(.inputtype("row")) ledbar_2: pin names not known; wires that end beside it: ledbar_2_p1
  assign controlled_buffer_1_out = not_1_out ? {8{1'b0}} : 8'bz;  // Controlled_Buffer controlled_buffer_1
  not not_1 (not_1_out, n_CONST_OE_00);
  alu alu_1 (
    .n_ALU_CS(n_ALU_CS), .n_ALU_CC(n_ALU_CC), .ALU_NAND(ALU_NAND), .ALU_D_NEG(ALU_SUB),
    .D_BUS(controlled_buffer_1_out), .n_CLK(n_CLK), .n_ALU_EN(n_ALU_EN), .ALU_RESET(ALU_CLR),
    .n_ALU_OE(n_ALU_OE), .n_ALU_ROR_OE(ASR_OE), .n_ALU_CF(n_CF), .n_ALU_ZF(n_ZF),
    .ALU_D_OUT(controlled_buffer_1_out), .ALU_OUT_ALWAYS(ledbar_2_p1));
  Pull_Resistor pull_resistor_1 (.node(controlled_buffer_1_out));
  instruction_reg instruction_reg_1 (
    .n_INC(CLK), .n_CLR(n_IRX_CLR), .D_BUS(controlled_buffer_1_out), .n_IR_WE(or_1_out), .IR_OUT(ledbar_1_p1));
  Clock clock_1 (.out(CLK));
  not not_2 (n_CLK, CLK);
  not not_3 (not_3_out, rom_1_data[3]);
  // LedBar #(.inputtype("row"), .matrixcols(16)) PC: pin names not known; wires that end beside it: PC_p1
  // LedBar #(.inputtype("row"), .matrixcols(16)) MAR: pin names not known; wires that end beside it: MAR_p1
  not not_4 (n_CONST_OE_00, decoder_1_out0);
  not not_5 (n_RAM_OE, decoder_1_out1);
  not not_6 (n_ALU_OE, decoder_1_out2);
  not not_7 (n_PCOUT_L, decoder_1_out3);
  not not_8 (n_PCOUT_H, decoder_1_out4);
  not not_9 (ASR_OE, decoder_1_out5);
  not not_10 (n_RF_OE, decoder_1_out6);
  not not_11 (n_ED_OE, decoder_1_out7);
  Decoder #(.select(3)) decoder_1 (
    .out0(decoder_1_out0), .out1(decoder_1_out1), .out2(decoder_1_out2), .out3(decoder_1_out3),
    .out4(decoder_1_out4), .out5(decoder_1_out5), .out6(decoder_1_out6), .out7(decoder_1_out7),
    .sel(rom_1_data[2:0]), .en(not_3_out));
  assign controlled_buffer_1_out = not_12_out ? {8{1'b1}} : 8'bz;  // Controlled_Buffer controlled_buffer_2
  not not_12 (not_12_out, n_CONST_OE_FF);
  Decoder #(.enable("false"), .select(3)) decoder_2 (
    .out0(decoder_2_out0), .out1(decoder_2_out1), .out2(decoder_2_out2), .out3(decoder_2_out3),
    .out4(decoder_2_out4), .out5(decoder_2_out5), .out6(decoder_2_out6), .out7(decoder_2_out7),
    .sel(rom_1_data[6:4]));
  address_controller address_controller_1 (
    .n_PCH_OUT(n_PCOUT_H), .n_PCL_OUT(n_PCOUT_L), .n_PC_LOAD(n_PC_LOAD), .CLK(CLK), .n_PC_CLEAR(1'b1),
    .PC_COUNT(PC_COUNT), .MAR_SEL(MAR_SEL), .DB_IN(controlled_buffer_1_out), .n_MAR_H(n_MARH_L),
    .n_MAR_L(n_MARL_L), .D_BUS(controlled_buffer_1_out),
    .ADDR_OUT({address_controller_1_addr_out, TTYI, TTYO}), .PC_OUT(PC_p1), .MAR_OUT(MAR_p1));
  // NOT_Gate not_13 has open pins: in=decoder_2_out0, out=open
  not not_14 (n_IR_WE, decoder_2_out1);
  not not_15 (n_RAM_WE, decoder_2_out2);
  not not_16 (n_RF_WE, decoder_2_out3);
  not not_17 (n_ALU_EN, decoder_2_out4);
  not not_18 (n_MARL_L, decoder_2_out5);
  not not_19 (n_MARH_L, decoder_2_out6);
  not not_20 (n_ED_WE, decoder_2_out7);
  nor nor_1 (nor_1_out, n_JEQ, n_ZF);
  nor nor_2 (nor_2_out, n_JCS, n_CF);
  Comparator #(.mode("unsigned"), .width(16)) comparator_1 (
    .a({address_controller_1_addr_out, TTYI, TTYO}), .b(16'h7ff), .lt(comparator_1_lt));  // open: gt, eq
  not not_21 (n_JMP, decoder_3_out0);
  not not_22 (n_JEQ, decoder_3_out1);
  not not_23 (n_JCS, decoder_3_out2);
  not not_24 (n_IRX_CLR, decoder_3_out3);
  not not_25 (n_ALU_CS, decoder_3_out4);
  not not_26 (n_ALU_CC, decoder_3_out5);
  not not_27 (n_CONST_OE_FF, decoder_3_out6);
  not not_28 (not_28_out, decoder_3_out7);
  Decoder #(.select(3)) decoder_3 (
    .out0(decoder_3_out0), .out1(decoder_3_out1), .out2(decoder_3_out2), .out3(decoder_3_out3),
    .out4(decoder_3_out4), .out5(decoder_3_out5), .out6(decoder_3_out6), .out7(decoder_3_out7),
    .sel(rom_1_data[2:0]), .en(rom_1_data[3]));
  nor nor_3 (nor_3_out, nor_1_out, nor_2_out);
  or or_2 (or_2_out, n_RAM_WE, n_CLK);
  not not_29 (not_29_out, comparator_1_lt);
  // LedBar #(.inputtype("row")) ledbar_3: pin names not known; wires that end beside it: controlled_buffer_1_out
  or or_3 (or_3_out, n_RF_WE, n_CLK);
  not not_30 (not_30_out, n_JMP);
  not not_31 (not_31_out, nor_3_out);
  nor nor_4 (nor_4_out, n_RAM_OE, comparator_1_lt);
  nor nor_5 (nor_5_out, n_RAM_OE, not_29_out);
  nor nor_6 (n_PC_LOAD, not_30_out, not_31_out);
  RAM #(.addrWidth(16), .trigger("low"), .\type ("nonvolatile")) ram_1 (
    .addr({address_controller_1_addr_out, TTYI, TTYO}), .we(or_2_out), .oe(nor_4_out),
    .din(controlled_buffer_1_out), .dout(ram_1_dout));
  ROM #(.addrWidth(16)) rom_2 (.addr({address_controller_1_addr_out, TTYI, TTYO}), .data(rom_2_data));
  and and_1 (and_1_out, TTYO, not_32_out);
  not not_32 (not_32_out, n_ED_WE);
  Bit_Extender #(.out_width(7)) bit_extender_1 (.in(controlled_buffer_1_out), .out(bit_extender_1_out));
  TTY tty_1 (.data(bit_extender_1_out), .clk(CLK), .we(and_1_out));  // open: clr
  not not_33 (not_33_out, n_ED_OE);
  reg_file reg_file_1 (
    .RF_OUT_0(RF_OUT_0), .RF_OUT_1(RF_OUT_1), .RF_IN_0(RF_IN_0), .RF_IN_1(RF_IN_1),
    .DB_IN(controlled_buffer_1_out), .n_EW(or_3_out), .n_ER(n_RF_OE), .DB_OUT(controlled_buffer_1_out),
    .RA(reg_file_1_ra), .RB(reg_file_1_rb), .RC(reg_file_1_rc), .RD(reg_file_1_rd));
  // LedBar #(.inputtype("row")) ledbar_4: pin names not known; wires that end beside it: reg_file_1_ra, CLK, n_ED_WE, n_ED_OE
  // LedBar #(.inputtype("row")) ledbar_5: pin names not known; wires that end beside it: reg_file_1_rb
  // LedBar #(.inputtype("row")) ledbar_6: pin names not known; wires that end beside it: reg_file_1_rc
  // LedBar #(.inputtype("row")) ledbar_7: pin names not known; wires that end beside it: reg_file_1_rd
  Keyboard #(.trigger("falling")) keyboard_1 (
    .clk(CLK), .re(and_2_out), .clr(in_1), .data(keyboard_1_data));  // open: avail
  and and_2 (and_2_out, TTYI, not_33_out);
  assign controlled_buffer_1_out = nor_4_out ? ram_1_dout : 8'bz;  // Controlled_Buffer controlled_buffer_3
  assign controlled_buffer_1_out = nor_5_out ? rom_2_data : 8'bz;  // Controlled_Buffer controlled_buffer_4
  assign controlled_buffer_5_out = not_33_out ? keyboard_1_data : 7'bz;  // Controlled_Buffer controlled_buffer_5
  assign controlled_buffer_1_out = {{1{controlled_buffer_5_out[6]}}, controlled_buffer_5_out};  // Bit_Extender bit_extender_2

  // Notes on the sheet:
  //   contents of rom_1 (hex, n*v repeats v):
  //   8011 b 30*0 8011 8051 8061 4076 b 27*0 8011 8c 41 8051 61 4c31 52 80 8041 62 40e1 3056 4076 b 18*0
  //   8011 8051 8061 8d 4037 46 b 25*0 8011 8c 51 8041 61 4c31 52 80 41 8062 4061 30d6 4037 46 b 17*0 8011
  //   80 140 8141 14e 32 b 25*0 8011 80 140 8051 8061 4141 14e 32 b 23*0 8011 8c 51 8041 61 4c31 52 80 41
  //   8062 4061 30d6 4041 32 b 17*0 8011 8c 51 8041 61 4c31 52 80 3046 1046 c32 80 41 8062 4061 30d6 4041
  //   32 b 13*0 8011 8c 51 8041 61 4c31 52 80 3046 2046 c32 80 41 8062 4061 30d6 4041 32 b 13*0 8011 8d
  //   1046 41 52 8080 41 62 808d 4041 32 b 20*0 8011 8d 2046 41 52 8080 41 62 808d 4041 32 b 20*0 8011 8d
  //   8041 432 b 27*0 8011 8d 8051 8061 4041 432 b 25*0 8011 8d 8041 832 b 27*0 8011 8d 8051 8061 4041 832
  //   b 25*0 8011 8051 8061 4026 b 27*0 8011 8c 41 8051 61 4c31 52 80 8041 62 40e1 3056 4026 b 18*0 8011
  //   8c 51 8041 61 4c31 52 80 3046 1046 c32 80 41 8062 4061 30d6 4026 b 14*0 8011 8c 51 8041 61 4c31 52
  //   80 3046 2046 c32 80 41 8062 4061 30d6 4026 b 14*0 8011 8d 8041 1046 52 80 8041 62 4026 b 22*0 8011
  //   8d 8041 2046 52 80 8041 62 4026 b 22*0 8011 8051 8061 5026 b 27*0 8011 8051 8061 6026 b 27*0 8011 8c
  //   46 32 b 27*0 8011 8c 1046 432 b 27*0 8011 8c 2046 832 b 27*0 8011 140 d 46 32 b 26*0 8011 140 d 1046
  //   432 b 26*0 8011 140 d 2046 832 b 26*0 8011 436 b 29*0 8011 8d 1046 1036 b 27*0 8011 8d 2046 2036 b
  //   27*0 8011 836 b 29*0 8011 1836 b 29*0 8011 2436 b 29*0 8011 8d 5e 6e 4031 4041 b 25*0 8011 8d 46 5e
  //   6e 4022 b 25*0 8011 c36 1036 3436 b 27*0 8011 c36 2036 3836 b 27*0 8011 1c36 2436 3836 b 27*0 8011 c
  //   b 29*0 8011 d b 29*0 8011 80 46 8041 32 b 26*0 8011 80d1 8061 46 4041 32 b 25*0 8011 80 46 40 32 8d
  //   1046 8041 52 80 8041 62 8d 4041 46 32 b 15*0 8011 80 46 40 32 8d 2046 8041 52 80 8041 62 8d 4041 46
  //   32 b 15*0 8011 80 46 1046 32 b 26*0 8011 80 46 2046 32 b 26*0 8011 140 146 14e 8241 32 b 25*0 8011
  //   140 146 14e 8051 8061 4241 32 b 23*0 8011 80 40 c32 8d 8041 1046 52 80 8041 62 8d 4e 3046 80 140 146
  //   14e 4241 32 b 11*0 8011 80 40 c32 8d 8041 2046 52 80 8041 62 8d 4e 3046 80 140 146 14e 4241 32 b
  //   11*0 8011 140 146 14e 1246 32 b 25*0 8011 140 146 14e 1246 32 b 25*0 8011 8d 46 8140 32 b 26*0 8011
  //   8051 8061 8d 46 4141 32 b 24*0 8011 8d 46 1146 32 b 26*0 8011 8d 46 2146 32 b 26*0 8011 8d 46 35 b
  //   27*0 8011 8d 46 35 8d 46 35 b 24*0 8011 8d 46 35 8d 46 35 8d 46 35 8d 46 35 b 18*0 8011 8d 46 8141
  //   14e 32 b 25*0 8011 8d 46 8051 8061 4141 14e 32 b 23*0 8011 8d 46 14e 32 8141 146 32 b 23*0 8011 8051
  //   8061 8d 46 14e 32 4141 146 32 b 21*0 8011 140 146 32 b 27*0 8011 8d 46 141 c32 146 32 8d 3046 8141
  //   146 32 b 19*0 8011 8051 8061 8d 4041 146 c32 146 32 8d 3046 4141 146 32 b 17*0 8011 8051 8061 4008 b
  //   27*0 8011 51 8c 8041 61 4c31 52 4061 b056 4008 b 21*0 8011 8051 8061 4009 b 27*0 8011 8051 8061 400a
  //   b 27*0 8011 5e 6e 140 d 240 4022 b 24*0 8011 8d 5e 6e 4041 8041 4022 b 24*0 8011 140 d 5e 6e 4041
  //   4022 c 40 52 4026 b 20*0 8011 140 d 5e 6e 4041 4022 c 40 52 5026 b 20*0 8011 140 d 5e 6e 4041 4022 c
  //   40 52 6026 b 20*0 8011 8c 5e 6e 4041 4022 52 8d 4041 32 b 21*0 8011 8c 5e 6e 4041 4022 52 8d 4041
  //   432 b 21*0 8011 8c 5e 6e 4041 4022 52 8d 4041 832 b 21*0 8011 5e 6e 140 d 4041 4051 4023 52 d 4024
  //   4e 5e 4022 8051 8061 4008 b 14*0 8011 8c 5e 6e 4041 52 4c31 c 40 52 4051 3066 4008 805e 806e 4022 b
  //   15*0 8011 5e 6e 8c 4041 8041 52 4031 8d 46 b 21*0 8011 5e 6e 8c 4041 8041 52 4c31 c 40 52 80 4061
  //   3056 4041 32 b 15*0 8011 5e 6e 8c 4041 8041 52 4c31 c 40 52 80 3046 1046 c32 80 4041 62 3056 8d 4041
  //   32 b 9*0 8011 5e 6e 8c 4041 8041 52 4c31 c 40 52 80 3046 2046 c32 80 4041 62 3056 8d 4041 32 b 9*0
  //   8011 5e 6e 8c 4041 8041 52 4026 b 23*0 8011 5e 6e 8c 4041 8041 52 4c31 c 40 52 80 4061 3056 4026 b
  //   16*0 8011 5e 6e 8c 4041 8041 52 4c31 c 40 52 80 3046 1046 c32 80 4041 62 3056 4026 b 11*0 8011 5e 6e
  //   8c 4041 8041 52 4c31 c 40 52 80 3046 2046 c32 80 4041 62 3056 4026 b 11*0 8011 8d 46 c 8241 b 26*0
  //   8011 8051 8061 8d 46 c 4241 b 24*0 8011 8d 1046 c 8241 b 26*0 8011 8d 1046 c 8051 8061 4241 b 24*0
  //   8011 8d 2046 c 8241 b 26*0 8011 8d 2046 c 8051 8061 4241 b 24*0 8011 8051 8061 4020 b 27*0 8011 8d
  //   46 8141 14e b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
  //   contents of rom_2 (hex, n*v repeats v):
  //   49 66 0 66 27 51 16 0 4a 2 66 0 66 37 51 16 0 4a 2 45 13 0 4c c 0 55 3 47 25 0 1 1 0 19 45 19 0 4f
  //   52 48 65 6c 6c 6f 2c 20 57 6f 72 6c 64 21 a d 0 49 27 6d 20 74 68 65 20 73 65 63 6f 6e 64 20 73 74
  //   72 69 6e 67 21 a d
endmodule

module address_controller (
  input  n_PCH_OUT,
  input  n_PCL_OUT,
  input  n_PC_LOAD,
  input  CLK,
  input  n_PC_CLEAR,
  input  PC_COUNT,
  input  MAR_SEL,
  input  [7:0] DB_IN,
  input  n_MAR_H,
  input  n_MAR_L,
  output [7:0] D_BUS,
  output [15:0] ADDR_OUT,
  output [15:0] PC_OUT,
  output [15:0] MAR_OUT
);

  wire and_1_out, buffer_1_out, buffer_2_out, counter_2_carry, nor_1_out, nor_2_out, not_1_out, not_2_out,
       not_3_out, not_4_out, not_5_out;

  not not_1 (not_1_out, n_PC_LOAD);
  buf buffer_1 (buffer_1_out, CLK);
  not not_2 (not_2_out, CLK);
  nor nor_1 (nor_1_out, not_2_out, n_MAR_H);
  nor nor_2 (nor_2_out, not_2_out, n_MAR_L);
  buf buffer_2 (buffer_2_out, buffer_1_out);
  not not_3 (not_3_out, n_PC_CLEAR);
  not not_4 (not_4_out, n_PCH_OUT);
  not not_5 (not_5_out, n_PCL_OUT);
  Counter counter_1 (
    .load(not_1_out), .D(ADDR_OUT[15:8]), .count(and_1_out), .Q(PC_OUT[15:8]), .clk(buffer_2_out),
    .clr(not_3_out));  // open: carry, up
  Counter counter_2 (
    .load(not_1_out), .D(ADDR_OUT[7:0]), .count(PC_COUNT), .Q(PC_OUT[7:0]), .carry(counter_2_carry),
    .clk(CLK), .clr(not_3_out));  // open: up
  and and_1 (and_1_out, counter_2_carry, PC_COUNT);
  assign D_BUS = not_4_out ? PC_OUT[15:8] : 8'bz;  // Controlled_Buffer controlled_buffer_1
  assign D_BUS = not_5_out ? PC_OUT[7:0] : 8'bz;  // Controlled_Buffer controlled_buffer_2
  reg_chip reg_chip_1 (.D_IN(DB_IN), .CLK(nor_1_out), .n_RESET(n_PC_CLEAR), .D_OUT(MAR_OUT[15:8]));
  reg_chip reg_chip_2 (.D_IN(DB_IN), .CLK(nor_2_out), .n_RESET(n_PC_CLEAR), .D_OUT(MAR_OUT[7:0]));
  Multiplexer #(.width(16)) multiplexer_1 (.in0(PC_OUT), .in1(MAR_OUT), .out(ADDR_OUT), .sel(MAR_SEL));
endmodule

module alu (
  input  n_ALU_CS,
  input  n_ALU_CC,
  input  ALU_NAND,
  input  ALU_D_NEG,
  input  [7:0] D_BUS,
  input  n_CLK,
  input  n_ALU_EN,
  input  ALU_RESET,
  input  n_ALU_OE,
  input  n_ALU_ROR_OE,
  output n_ALU_CF,
  output n_ALU_ZF,
  output [7:0] ALU_D_OUT,
  output [7:0] ALU_OUT_ALWAYS
);

  wire adder_1_cout, comparator_1_eq, d_ff_1_q, nor_1_out, nor_2_out, not_1_out, not_2_out, not_3_out,
       not_4_out, not_5_out, not_6_out, not_8_out;
  wire [2:0] bit_extender_2_out;
  wire [7:0] adder_1_out, bit_extender_1_out, multiplexer_1_out, nand_1_out, shifter_1_out, xor_1_out;

  nor nor_1 (nor_1_out, n_CLK, n_ALU_EN);
  assign bit_extender_1_out = {{7{ALU_D_NEG}}, ALU_D_NEG};  // Bit_Extender bit_extender_1
  not not_1 (not_1_out, nor_1_out);
  not not_2 (not_2_out, ALU_RESET);
  not not_3 (not_3_out, n_ALU_ROR_OE);
  not not_4 (not_4_out, ALU_NAND);
  assign xor_1_out = bit_extender_1_out ^ D_BUS;  // XOR_Gate xor_1, 8 bits wide
  nor nor_2 (nor_2_out, ALU_NAND, not_1_out);
  assign bit_extender_2_out = {{2{1'b0}}, not_3_out};  // Bit_Extender bit_extender_2
  assign nand_1_out = ~(D_BUS & ALU_OUT_ALWAYS);  // NAND_Gate nand_1, 8 bits wide
  Adder adder_1 (.a(xor_1_out), .b(ALU_OUT_ALWAYS), .out(adder_1_out), .cin(d_ff_1_q), .cout(adder_1_cout));
  reg_chip reg_chip_1 (.D_IN(multiplexer_1_out), .CLK(nor_1_out), .n_RESET(not_2_out), .D_OUT(ALU_OUT_ALWAYS));
  Shifter #(.shift("rr")) shifter_1 (.in(ALU_OUT_ALWAYS), .\dist (bit_extender_2_out), .out(shifter_1_out));
  not not_5 (not_5_out, n_ALU_CS);
  not not_6 (not_6_out, n_ALU_CC);
  Multiplexer #(.width(8)) multiplexer_1 (
    .in0(nand_1_out), .in1(adder_1_out), .out(multiplexer_1_out), .sel(not_4_out));
  assign ALU_D_OUT = not_3_out ? shifter_1_out : 8'bz;  // Controlled_Buffer controlled_buffer_1
  D_Flip_Flop d_ff_1 (
    .D(adder_1_cout), .clk(nor_2_out), .Q(d_ff_1_q), .Qn(n_ALU_CF), .preset(not_5_out), .reset(not_6_out));
  Comparator comparator_1 (.a({8{1'b0}}), .b(ALU_OUT_ALWAYS), .eq(comparator_1_eq));  // open: gt, lt
  // LedBar #(.inputtype("row")) ledbar_1: pin names not known; wires that end beside it: multiplexer_1_out
  not not_7 (n_ALU_ZF, comparator_1_eq);
  assign ALU_D_OUT = not_8_out ? ALU_OUT_ALWAYS : 8'bz;  // Controlled_Buffer controlled_buffer_2
  not not_8 (not_8_out, n_ALU_OE);
endmodule

module reg_chip (
  input  [7:0] D_IN,
  input  CLK,
  input  n_RESET,
  output [7:0] D_OUT
);

  wire not_1_out;

  not not_1 (not_1_out, n_RESET);
  Register register_1 (.D(D_IN), .en(CLK), .clk(CLK), .Q(D_OUT), .clr(not_1_out));
endmodule

module reg_file (
  input  RF_OUT_0,
  input  RF_OUT_1,
  input  RF_IN_0,
  input  RF_IN_1,
  input  [7:0] DB_IN,
  input  n_EW,
  input  n_ER,
  output [7:0] DB_OUT,
  output [7:0] RA,
  output [7:0] RB,
  output [7:0] RC,
  output [7:0] RD
);

  wire and_1_out, and_2_out, and_3_out, and_4_out, decoder_1_out0, decoder_1_out1, decoder_1_out2,
       decoder_1_out3, decoder_2_out0, decoder_2_out1, decoder_2_out2, decoder_2_out3, not_1_out;

  Decoder #(.enable("false"), .select(2)) decoder_1 (
    .out0(decoder_1_out0), .out1(decoder_1_out1), .out2(decoder_1_out2), .out3(decoder_1_out3),
    .sel({RF_IN_1, RF_IN_0}));
  Decoder #(.enable("false"), .select(2)) decoder_2 (
    .out0(decoder_2_out0), .out1(decoder_2_out1), .out2(decoder_2_out2), .out3(decoder_2_out3),
    .sel({RF_OUT_1, RF_OUT_0}));
  Register #(.trigger("low")) register_1 (.D(DB_IN), .en(decoder_1_out0), .clk(n_EW), .Q(RA));  // open: clr
  Register #(.trigger("low")) register_2 (.D(DB_IN), .en(decoder_1_out1), .clk(n_EW), .Q(RB));  // open: clr
  Register #(.trigger("low")) register_3 (.D(DB_IN), .en(decoder_1_out2), .clk(n_EW), .Q(RC));  // open: clr
  Register #(.trigger("low")) register_4 (.D(DB_IN), .en(decoder_1_out3), .clk(n_EW), .Q(RD));  // open: clr
  not not_1 (not_1_out, n_ER);
  and and_1 (and_1_out, not_1_out, decoder_2_out1);
  and and_2 (and_2_out, not_1_out, decoder_2_out0);
  assign DB_OUT = and_2_out ? RA : 8'bz;  // Controlled_Buffer controlled_buffer_1
  and and_3 (and_3_out, not_1_out, decoder_2_out2);
  and and_4 (and_4_out, not_1_out, decoder_2_out3);
  assign DB_OUT = and_1_out ? RB : 8'bz;  // Controlled_Buffer controlled_buffer_2
  assign DB_OUT = and_3_out ? RC : 8'bz;  // Controlled_Buffer controlled_buffer_3
  assign DB_OUT = and_4_out ? RD : 8'bz;  // Controlled_Buffer controlled_buffer_4
endmodule

module instruction_reg (
  input  n_INC,
  input  n_CLR,
  input  [7:0] D_BUS,
  input  n_IR_WE,
  output [11:0] IR_OUT
);

  wire buffer_1_out, buffer_2_out, not_1_out, not_2_out, not_3_out;
  wire [7:0] reg_chip_1_d_out;

  not not_1 (not_1_out, n_IR_WE);
  buf buffer_1 (buffer_1_out, n_INC);
  buf buffer_2 (buffer_2_out, buffer_1_out);
  not not_2 (not_2_out, n_CLR);
  not not_3 (not_3_out, buffer_2_out);
  Counter #(.max('h1f), .width(5)) counter_1 (
    .count(1'b1), .Q(IR_OUT[4:0]), .clk(not_3_out), .clr(not_2_out));  // open: load, D, carry, up
  reg_chip reg_chip_1 (.D_IN(D_BUS), .CLK(not_1_out), .n_RESET(n_CLR), .D_OUT(reg_chip_1_d_out));
  Bit_Extender #(.out_width(7), .\type ("zero")) bit_extender_1 (.in(reg_chip_1_d_out), .out(IR_OUT[11:5]));
endmodule

module ram_chip (
  input  [15:0] ADDR_IN,
  input  n_WE,
  input  n_OE,
  input  [7:0] DB_IN,
  output [7:0] DB_OUT
);

  wire not_1_out;

  not not_1 (not_1_out, n_OE);
  RAM #(.addrWidth(16), .trigger("low"), .\type ("nonvolatile")) ram_1 (
    .addr(ADDR_IN), .we(n_WE), .oe(not_1_out), .din(DB_IN), .dout(DB_OUT));
endmodule

module mem_module (
  input  [7:0] DB_IN,
  input  [15:0] ADDR_IN,
  input  n_MEM_OE,
  input  n_RAM_WE,
  output [7:0] DB_OUT
);

  wire comparator_1_lt, nor_1_out, nor_2_out, not_1_out;
  wire [7:0] ram_1_dout, rom_1_data;

  Comparator #(.mode("unsigned"), .width(16)) comparator_1 (
    .a(ADDR_IN), .b(16'h7ff), .lt(comparator_1_lt));  // open: gt, eq
  not not_1 (not_1_out, comparator_1_lt);
  nor nor_1 (nor_1_out, n_MEM_OE, comparator_1_lt);
  nor nor_2 (nor_2_out, n_MEM_OE, not_1_out);
  RAM #(.addrWidth(16), .trigger("low"), .\type ("nonvolatile")) ram_1 (
    .addr(ADDR_IN), .we(n_RAM_WE), .din(DB_IN), .dout(ram_1_dout));  // open: oe
  ROM #(.addrWidth(16)) rom_1 (.addr(ADDR_IN), .data(rom_1_data));
  assign DB_OUT = nor_1_out ? ram_1_dout : 8'bz;  // Controlled_Buffer controlled_buffer_1
  assign DB_OUT = nor_2_out ? rom_1_data : 8'bz;  // Controlled_Buffer controlled_buffer_2

  // Notes on the sheet:
  //   contents of rom_1 (hex, n*v repeats v):
  //   0 3 a3 125*0 41
endmodule
